# Fritzing sketch green-hill-HVAC (saved by Fritzing 0.9.3b)
breadboards: 1

parts:
  Part1 = Arduino Uno (Rev3)
  R1 = Resistor [tolerance=±5% resistance=220 package="1206 [SMD]"]
  LED1 = smd LED [color="Red (633nm)" package="0805 [SMD]"]
  LED2 = smd LED [color="Red (633nm)" package="0805 [SMD]"]
  Grove1 = Grove OLED 128x96
  S2 = Momentary Switch [package=ksa_sealed_tac_switch]
  S3 = Momentary Switch [package=ksa_sealed_tac_switch]
  R4 = Resistor [tolerance=±5% resistance=220 package="1206 [SMD]"]
  R5 = Resistor [tolerance=±5% resistance=220 package="1206 [SMD]"]
  MQ-9 = GAS_SENSOR [package=mq-3]
  MQ-135 = GAS_SENSOR [package=mq-3]
  R6 = Resistor [tolerance=±5% resistance=220 package="1206 [SMD]"]
  R7 = Temperature Sensor (Thermistor) [thermistor_type=NTC package=THT]
  R_load = Resistor [tolerance=±5% resistance=10k package=THT]
  U1 = RELAY [package=relay-jzc]
  U2 = RELAY [package=relay-jzc]
  VCC1 = Battery

nets:
  N1: Part1.A0, MQ-135.A0
  N2: Part1.A1, MQ-9.D0, MQ-9.A0
  N3: Part1.A3, R7.pin_1, R_load.Pin_0
  N4: Part1.A4/SDA, Grove1.SDA
  N5: Part1.A5/SCL, Grove1.SCL
  GND: Part1.GND, Grove1.GND, R4.Pin_1
  N6: Part1.D2, S2.1, R6.Pin_0
  N7: Part1.D3_PWM, S3.1, R4.Pin_0
  N8: Part1.D4, R1.Pin_0
  N9: Part1.D5_PWM, R5.Pin_0
  3V3: Part1.3V3, Grove1.VCC
  5V: Part1.5V, MQ-135.VCC
  N10: R1.Pin_1, LED2.anode
  N11: LED1.cathode, LED2.cathode, MQ-135.GND
  N12: LED1.anode, R5.Pin_1, U2.NO
  N13: U1.COIL1, VCC1.+
  N14: U2.MAIN, VCC1.-

notes:
  A0 -analog outputs
  screen
  fan
  relay_1
  relay_2
  NO to Fan1
  NO to Fan2
  CO2
  CH4

custom parts:
  GAS_SENSOR: MQ-3 alcohol gas sensor . FP not tested. SEN-08880.
